# Fritzing sketch ArduinoBLETemperature (saved by Fritzing 0.9.3b)
breadboards: 1

parts:
  Part1 = Arduino Uno (Rev3)
  T1 = LM35 Temperature Sensor [package="TO92 [THT]"]
  Part2 = Bluetooth HC-05 Macho  # not connected

nets:
  N1: Part1.A0, T1.Vout
  N2: Part1.5V, T1.+Vs
  GND: Part1.GND, T1.GND

notes:
  HC-08
